# Fritzing sketch fourmotors (saved by Fritzing 0.9.3b)
breadboards: 1

parts:
  9V = 4 x AAA Battery Mount
  DRV1 = X113647 Stepper Driver Board [package=board]
  DRV2 = X113647 Stepper Driver Board [package=board]
  DRV4 = X113647 Stepper Driver Board [package=board]
  DRV3 = X113647 Stepper Driver Board [package=board]
  MTR1 = 28BYJ-48 Stepper Motor
  MTR2 = 28BYJ-48 Stepper Motor
  MTR4 = 28BYJ-48 Stepper Motor
  MTR3 = 28BYJ-48 Stepper Motor
  ARDUINO_NANO = Arduino Nano (Rev3.0) (ICSP)

nets:
  GND: 9V.-, DRV1.GND, DRV2.GND, DRV4.GND, DRV3.GND, ARDUINO_NANO.GND
  N1: 9V.+, DRV1.+V, DRV2.+V, DRV4.+V, DRV3.+V
  N2: DRV1.IN1, DRV2.IN1, DRV4.IN1, DRV3.IN1, ARDUINO_NANO.D5
  N3: DRV1.IN2, DRV2.IN2, DRV4.IN2, DRV3.IN2, ARDUINO_NANO.D4
  N4: DRV1.IN3, DRV2.IN3, DRV4.IN3, DRV3.IN3, ARDUINO_NANO.D3
  N5: DRV1.IN4, DRV2.IN4, DRV4.IN4, DRV3.IN4, ARDUINO_NANO.D2
  N6: DRV1.BLUE, MTR1.BLUE
  N7: DRV1.PINK, MTR1.PINK
  N8: DRV1.YELLOW, MTR1.YELLOW
  N9: DRV1.ORANGE, MTR1.ORANGE
  N10: DRV1.RED, MTR1.RED
  N11: DRV2.BLUE, MTR2.BLUE
  N12: DRV2.PINK, MTR2.PINK
  N13: DRV2.YELLOW, MTR2.YELLOW
  N14: DRV2.ORANGE, MTR2.ORANGE
  N15: DRV2.RED, MTR2.RED
  N16: DRV4.BLUE, MTR4.BLUE
  N17: DRV4.PINK, MTR4.PINK
  N18: DRV4.YELLOW, MTR4.YELLOW
  N19: DRV4.ORANGE, MTR4.ORANGE
  N20: DRV4.RED, MTR4.RED
  N21: DRV3.BLUE, MTR3.BLUE
  N22: DRV3.PINK, MTR3.PINK
  N23: DRV3.YELLOW, MTR3.YELLOW
  N24: DRV3.ORANGE, MTR3.ORANGE
  N25: DRV3.RED, MTR3.RED

notes:
  Bionic arm, 4 motors to control digit II-V. This way the hand moves like mittens., 1

custom parts:
  X113647 Stepper Driver Board: A common stepper motor driver board based on ULN2003APG darlington array
  28BYJ-48 Stepper Motor: 28BYJ-48 gear-reduction stepper motor (small)
